# Fritzing sketch wiring_fritzing (saved by Fritzing 0.9.4)

parts:
  Part1 = Arduino Nano (Rev3.0)
  Grove1 = Grove OLED 128x96
  HC-SR04_Sensor_1 = HC-SR04 Ultrasonic Distance Sensor
  U1 = MLX90614 [package=to-39]
  J1 = Piezo Speaker  # not connected
  R1 = Resistor [tolerance=±5% resistance=220 package="2010 [SMD]"]

nets:
  GND: Part1.GND, HC-SR04_Sensor_1.GND, U1.VSS
  N1: Part1.D2, HC-SR04_Sensor_1.ECHO
  N2: Part1.D3, HC-SR04_Sensor_1.TRIG
  N3: Part1.VIN, R1.Pin_1
  N4: Part1.A5, U1.SCL_VZ
  N5: Part1.A4, Grove1.SDA
  3V3: Part1.3V3, HC-SR04_Sensor_1.VCC, U1.VDD

notes:
  Ultrasonic sensor
  OLED display
  IR sensor
  piezo buzzer
  GND
  I/O
  VCC
  Note:  Here only buzzer is shown
  as module diagram was not found
  SDA
  SCL
  Developed at:
  Parikalpana Nepal
  Project link:
  https://github.com/m3kamal/infrared-thermometer
